// Logisim project ULA_ARQ.circ as structural Verilog: 9 circuits, main circuit main
// ULA
module main (
);

  ULA ula_1 ();  // open: OpALU, Result, A, Shamt, B, ZERO, Overflow
endmodule

module ULA (
  input  [31:0] A,
  input  [31:0] B,
  input  [4:0] Shamt,
  input  [3:0] OpALU,
  output ZERO,
  output [31:0] Result,
  output Overflow
);

  wire and_2_out, and_3_out, and_4_out, and_5_out, comparator_1_lt, overflow_add_overflow,
       overflow_sub_1_overflow;
  wire [31:0] adder_1_out, and_1_out, extensor_1_out_2, nor_1_out, or_1_out, shifter_1_out, shifter_2_out,
       subtractor_1_out, xor_1_out;

  assign and_1_out = A & B;  // AND_Gate and_1, 32 bits wide
  assign or_1_out = A | B;  // OR_Gate or_1, 32 bits wide
  assign nor_1_out = ~(A | B);  // NOR_Gate nor_1, 32 bits wide
  assign xor_1_out = A ^ B;  // XOR_Gate xor_1, 32 bits wide
  Comparator #(.width(32)) comparator_1 (.a(A), .b(B), .lt(comparator_1_lt));  // open: gt, eq
  Adder #(.width(32)) adder_1 (.a(A), .b(B), .out(adder_1_out));  // open: cin, cout
  Subtractor #(.width(32)) subtractor_1 (.a(A), .b(B), .out(subtractor_1_out));  // open: bin, bout
  Shifter #(.width(32)) shifter_1 (.in(A), .\dist (Shamt), .out(shifter_1_out));
  Shifter #(.width(32), .shift("lr")) shifter_2 (.in(A), .\dist (Shamt), .out(shifter_2_out));
  extensor extensor_1 (.in_1(comparator_1_lt), .out_2(extensor_1_out_2));
  overflow_sub overflow_sub_1 (.a(A), .b(B), .res(subtractor_1_out), .overflow(overflow_sub_1_overflow));
  overflow overflow_add (.overflow(overflow_add_overflow), .a(A), .res(adder_1_out), .b(B));
  pega_zero pega_zero_1 (.in_1(Result), .out_2(ZERO));
  Multiplexer #(.select(4), .width(32), .enable("false")) multiplexer_1 (
    .in0(and_1_out), .in1(or_1_out), .in2(nor_1_out), .in3(xor_1_out), .in4(extensor_1_out_2),
    .in5(adder_1_out), .in6(subtractor_1_out), .in7(shifter_1_out), .in8(shifter_2_out), .out(Result),
    .sel(OpALU));  // open: in9, in10, in11, in12, in13, in14, in15
  and and_2 (and_2_out, OpALU[0], ~OpALU[1], OpALU[2], ~OpALU[3]);  // AND_Gate
  and and_3 (and_3_out, ~OpALU[0], OpALU[1], OpALU[2], ~OpALU[3]);  // AND_Gate
  and and_4 (and_4_out, and_2_out, overflow_add_overflow);
  buf and_5 (and_5_out, and_3_out);  // AND_Gate
  or or_2 (Overflow, and_4_out, and_5_out);
endmodule

module BR (
  input  [31:0] WD,
  input  regWrite,
  input  [1:0] LR1,
  input  [1:0] WR,
  input  [1:0] LR2,
  output [31:0] LD1,
  output [31:0] LD2
);

  wire clock_1_out, demultiplexer_1_out0, demultiplexer_1_out1, demultiplexer_1_out2, demultiplexer_1_out3;
  wire [31:0] _00_2_q, _00_q, _01_2_q, _01_q, _10_2_q, _10_q, _11_2_q, _11_q;

  Clock clock_1 (.out(clock_1_out));
  Demultiplexer #(.select(2)) demultiplexer_1 (
    .out0(demultiplexer_1_out0), .out1(demultiplexer_1_out1), .out2(demultiplexer_1_out2),
    .out3(demultiplexer_1_out3), .in(regWrite), .sel(WR));  // open: en
  Register #(.width(32)) _00 (.D(WD), .en(demultiplexer_1_out0), .Q(_00_q), .clk(clock_1_out));  // open: clr
  Register #(.width(32)) _01 (.D(WD), .en(demultiplexer_1_out1), .Q(_01_q), .clk(clock_1_out));  // open: clr
  Register #(.width(32)) _10 (.D(WD), .en(demultiplexer_1_out2), .Q(_10_q), .clk(clock_1_out));  // open: clr
  Register #(.width(32)) _11 (.D(WD), .en(demultiplexer_1_out3), .Q(_11_q), .clk(clock_1_out));  // open: clr
  Register #(.width(32)) _00_2 (.D(WD), .Q(_00_2_q), .clk(clock_1_out));  // open: en, clr
  Register #(.width(32)) _01_2 (.D(WD), .Q(_01_2_q), .clk(clock_1_out));  // open: en, clr
  Register #(.width(32)) _10_2 (.D(WD), .Q(_10_2_q), .clk(clock_1_out));  // open: en, clr
  Register #(.width(32)) _11_2 (.D(WD), .Q(_11_2_q), .clk(clock_1_out));  // open: en, clr
  Multiplexer #(.select(2), .width(32)) multiplexer_1 (
    .in0(_00_q), .in1(_01_q), .in2(_10_q), .in3(_11_q), .out(LD1), .sel(LR1));  // open: en
  Multiplexer #(.select(2), .width(32)) multiplexer_2 (
    .in0(_00_2_q), .in1(_01_2_q), .in2(_10_2_q), .in3(_11_2_q), .out(LD2), .sel(LR2));  // open: en
endmodule

module pega_zero (
  input  [31:0] in_1,
  output out_2
);

  nor nor_1 (out_2, in_1[0], in_1[1], in_1[2], in_1[3], in_1[4], in_1[5], in_1[6], in_1[7], in_1[8], in_1[9], in_1[10], in_1[11], in_1[12], in_1[13], in_1[14], in_1[15], in_1[16], in_1[17], in_1[18], in_1[19], in_1[20], in_1[21], in_1[22], in_1[23], in_1[24], in_1[25], in_1[26], in_1[27], in_1[28], in_1[29], in_1[30], in_1[31]);
endmodule

module decodificador (
  input  [31:0] in_1,
  output [5:0] funct,
  output [4:0] shamt,
  output [4:0] rd,
  output [15:0] imm,
  output [4:0] rt,
  output [25:0] addr,
  output [4:0] rs,
  output [5:0] opcode
);


  assign funct = in_1[5:0];
  assign opcode = in_1[31:26];
  assign rd = in_1[15:11];
  assign rs = in_1[25:21];
  assign rt = in_1[20:16];
  assign shamt = in_1[10:6];
endmodule

module extensor (
  input  in_1,
  output [31:0] out_2
);


  assign out_2 = {32{in_1}};
endmodule

module ler_opcode (
  input  [5:0] in_1,
  output RegWrite,
  output RegDst
);

  nand nand_1 (RegDst, in_1[0], in_1[1], in_1[2], in_1[3], in_1[4], in_1[5]);

  assign RegWrite = RegDst;
endmodule

module overflow (
  input  [31:0] a,
  input  [31:0] b,
  input  [31:0] res,
  output overflow
);

  wire and_1_out, and_2_out, not_1_out, not_2_out, not_3_out;

  not not_1 (not_1_out, a[31]);
  not not_2 (not_2_out, b[31]);
  not not_3 (not_3_out, res[31]);
  and and_1 (and_1_out, not_1_out, not_2_out, res[31]);
  and and_2 (and_2_out, a[31], b[31], not_3_out);
  or or_1 (overflow, and_1_out, and_2_out);
endmodule

module overflow_sub (
  input  [31:0] a,
  input  [31:0] b,
  input  [31:0] res,
  output overflow
);

  wire and_1_out, and_2_out, not_1_out, not_2_out, not_3_out;

  not not_1 (not_1_out, a[31]);
  not not_2 (not_2_out, b[31]);
  not not_3 (not_3_out, res[31]);
  and and_1 (and_1_out, not_1_out, b[31], res[31]);
  and and_2 (and_2_out, a[31], not_2_out, not_3_out);
  or or_1 (overflow, and_1_out, and_2_out);
endmodule
