// Logisim project ULA_ARQ_NOVA.circ as structural Verilog: 9 circuits, main circuit main
// ULA
module main (
  input  [31:0] A,
  input  [31:0] A_2,
  input  [4:0] Shamt,
  input  [3:0] \Operação_ALU ,
  output Zero,
  output [31:0] Result,
  output Overflow
);

  ULA ula_1 (.OpALU(\Operação_ALU ), .Result(Result), .A(A), .Shamt(Shamt), .B(A_2), .out_5(Zero), .Overflow(Overflow));
endmodule

module ULA (
  input  [31:0] A,
  input  [31:0] B,
  input  [4:0] Shamt,
  input  [3:0] OpALU,
  output out_5,
  output [31:0] Result,
  output Overflow
);

  wire and_2_out, and_3_out, and_4_out, and_5_out, comparator_1_lt, overflow_add_overflow,
       overflow_sub_overflow;
  wire [31:0] adder_1_out, and_1_out, extensor_1_out_2, nor_1_out, or_1_out, shifter_1_out, shifter_2_out,
       subtractor_1_out, xor_1_out;

  // Probe on A
  // Probe on B
  assign and_1_out = A & B;  // AND_Gate and_1, 32 bits wide
  assign or_1_out = A | B;  // OR_Gate or_1, 32 bits wide
  assign nor_1_out = ~(A | B);  // NOR_Gate nor_1, 32 bits wide
  assign xor_1_out = A ^ B;  // XOR_Gate xor_1, 32 bits wide
  Comparator #(.width(32)) comparator_1 (.a(A), .b(B), .lt(comparator_1_lt));  // open: gt, eq
  extensor extensor_1 (.in_1(comparator_1_lt), .out_2(extensor_1_out_2));
  Adder #(.width(32)) adder_1 (.a(A), .b(B), .out(adder_1_out));  // open: cin, cout
  Subtractor #(.width(32)) subtractor_1 (.a(A), .b(B), .out(subtractor_1_out));  // open: bin, bout
  Shifter #(.width(32)) shifter_1 (.in(A), .\dist (Shamt), .out(shifter_1_out));
  Shifter #(.width(32), .shift("lr")) shifter_2 (.in(A), .\dist (Shamt), .out(shifter_2_out));
  overflow_sub overflow_sub (.a(A), .b(B), .res(subtractor_1_out), .overflow(overflow_sub_overflow));
  overflow overflow_add (.overflow(overflow_add_overflow), .a(A), .res(adder_1_out), .b(B));
  Multiplexer #(.select(4), .width(32)) multiplexer_1 (
    .in0(and_1_out), .in1(or_1_out), .in2(nor_1_out), .in3(xor_1_out), .in4(extensor_1_out_2),
    .in5(adder_1_out), .in6(subtractor_1_out), .in7(shifter_1_out), .in8(shifter_2_out), .out(Result),
    .sel(OpALU));  // open: in9, in10, in11, in12, in13, in14, in15, en
  pega_zero pega_zero_1 (.in_1(Result), .out_2(out_5));
  // Probe on OpALU
  and and_2 (and_2_out, OpALU[0], ~OpALU[1], OpALU[2], ~OpALU[3]);  // AND_Gate
  and and_3 (and_3_out, and_2_out, overflow_add_overflow);
  and and_4 (and_4_out, overflow_sub_overflow, and_5_out);
  and and_5 (and_5_out, ~OpALU[0], OpALU[1], OpALU[2], ~OpALU[3]);  // AND_Gate
  or or_2 (Overflow, and_3_out, and_4_out);
  // Probe on Result
endmodule

module BR (
  input  [31:0] WD,
  input  RegWrite,
  input  [4:0] LR1,
  input  [4:0] WR,
  input  [4:0] LR2,
  output [31:0] LD1,
  output [31:0] LD2
);

  wire clock_1_out, demultiplexer_1_out0, demultiplexer_1_out1, demultiplexer_1_out2, demultiplexer_1_out3,
       demultiplexer_1_out4, demultiplexer_1_out5, demultiplexer_1_out6, demultiplexer_1_out7,
       demultiplexer_1_out8, demultiplexer_1_out9, demultiplexer_1_out10, demultiplexer_1_out11,
       demultiplexer_1_out12, demultiplexer_1_out13, demultiplexer_1_out14, demultiplexer_1_out15,
       demultiplexer_1_out16, demultiplexer_1_out17, demultiplexer_1_out18, demultiplexer_1_out19,
       demultiplexer_1_out20, demultiplexer_1_out21, demultiplexer_1_out22, demultiplexer_1_out23,
       demultiplexer_1_out24, demultiplexer_1_out25, demultiplexer_1_out26, demultiplexer_1_out27,
       demultiplexer_1_out28, demultiplexer_1_out29, demultiplexer_1_out30, demultiplexer_1_out31,
       demultiplexer_2_out0, demultiplexer_2_out1, demultiplexer_2_out2, demultiplexer_2_out3,
       demultiplexer_2_out4, demultiplexer_2_out5, demultiplexer_2_out6, demultiplexer_2_out7,
       demultiplexer_2_out8, demultiplexer_2_out9, demultiplexer_2_out10, demultiplexer_2_out11,
       demultiplexer_2_out12, demultiplexer_2_out13, demultiplexer_2_out14, demultiplexer_2_out15,
       demultiplexer_2_out16, demultiplexer_2_out17, demultiplexer_2_out18, demultiplexer_2_out19,
       demultiplexer_2_out20, demultiplexer_2_out21, demultiplexer_2_out22, demultiplexer_2_out23,
       demultiplexer_2_out24, demultiplexer_2_out25, demultiplexer_2_out26, demultiplexer_2_out27,
       demultiplexer_2_out28, demultiplexer_2_out29, demultiplexer_2_out30, demultiplexer_2_out31;
  wire [31:0] _00000_2_q, _00000_q, _00001_2_q, _00001_q, _00010_2_q, _00010_q, _00011_2_q, _00011_q,
       _00100_2_q, _00100_q, _00101_2_q, _00101_q, _00110_2_q, _00110_q, _00111_2_q, _00111_q, _01000_2_q,
       _01000_q, _01001_2_q, _01001_q, _01010_2_q, _01010_q, _01011_2_q, _01011_q, _01100_2_q, _01100_q,
       _01101_2_q, _01101_q, _01110_2_q, _01110_q, _01111_2_q, _01111_q, _10000_2_q, _10000_q, _10001_2_q,
       _10001_q, _10010_2_q, _10010_q, _10011_2_q, _10011_q, _10100_2_q, _10100_q, _10101_2_q, _10101_q,
       _10110_2_q, _10110_q, _10111_2_q, _10111_q, _11000_2_q, _11000_q, _11001_2_q, _11001_q, _11010_2_q,
       _11010_q, _11011_2_q, _11011_q, _11100_2_q, _11100_q, _11101_2_q, _11101_q, _11110_2_q, _11110_q,
       and_1_out, and_2_out, undriven, undriven_2;

  // Probe on WD
  Demultiplexer #(.select(5)) demultiplexer_1 (
    .out0(demultiplexer_1_out0), .out1(demultiplexer_1_out1), .out2(demultiplexer_1_out2),
    .out3(demultiplexer_1_out3), .out4(demultiplexer_1_out4), .out5(demultiplexer_1_out5),
    .out6(demultiplexer_1_out6), .out7(demultiplexer_1_out7), .out8(demultiplexer_1_out8),
    .out9(demultiplexer_1_out9), .out10(demultiplexer_1_out10), .out11(demultiplexer_1_out11),
    .out12(demultiplexer_1_out12), .out13(demultiplexer_1_out13), .out14(demultiplexer_1_out14),
    .out15(demultiplexer_1_out15), .out16(demultiplexer_1_out16), .out17(demultiplexer_1_out17),
    .out18(demultiplexer_1_out18), .out19(demultiplexer_1_out19), .out20(demultiplexer_1_out20),
    .out21(demultiplexer_1_out21), .out22(demultiplexer_1_out22), .out23(demultiplexer_1_out23),
    .out24(demultiplexer_1_out24), .out25(demultiplexer_1_out25), .out26(demultiplexer_1_out26),
    .out27(demultiplexer_1_out27), .out28(demultiplexer_1_out28), .out29(demultiplexer_1_out29),
    .out30(demultiplexer_1_out30), .out31(demultiplexer_1_out31), .in(RegWrite), .sel(WR));  // open: en
  // Probe on WR
  Demultiplexer #(.select(5)) demultiplexer_2 (
    .out0(demultiplexer_2_out0), .out1(demultiplexer_2_out1), .out2(demultiplexer_2_out2),
    .out3(demultiplexer_2_out3), .out4(demultiplexer_2_out4), .out5(demultiplexer_2_out5),
    .out6(demultiplexer_2_out6), .out7(demultiplexer_2_out7), .out8(demultiplexer_2_out8),
    .out9(demultiplexer_2_out9), .out10(demultiplexer_2_out10), .out11(demultiplexer_2_out11),
    .out12(demultiplexer_2_out12), .out13(demultiplexer_2_out13), .out14(demultiplexer_2_out14),
    .out15(demultiplexer_2_out15), .out16(demultiplexer_2_out16), .out17(demultiplexer_2_out17),
    .out18(demultiplexer_2_out18), .out19(demultiplexer_2_out19), .out20(demultiplexer_2_out20),
    .out21(demultiplexer_2_out21), .out22(demultiplexer_2_out22), .out23(demultiplexer_2_out23),
    .out24(demultiplexer_2_out24), .out25(demultiplexer_2_out25), .out26(demultiplexer_2_out26),
    .out27(demultiplexer_2_out27), .out28(demultiplexer_2_out28), .out29(demultiplexer_2_out29),
    .out30(demultiplexer_2_out30), .out31(demultiplexer_2_out31), .in(RegWrite), .sel(WR));  // open: en
  // Probe on WR
  Clock clock_1 (.out(clock_1_out));
  Register #(.width(32)) _00000 (.D(WD), .en(demultiplexer_1_out0), .Q(_00000_q), .clk(clock_1_out));  // open: clr
  Register #(.width(32)) _00001 (.D(WD), .en(demultiplexer_1_out1), .Q(_00001_q), .clk(clock_1_out));  // open: clr
  Register #(.width(32)) _00010 (.D(WD), .en(demultiplexer_1_out2), .Q(_00010_q), .clk(clock_1_out));  // open: clr
  Register #(.width(32)) _00011 (.D(WD), .en(demultiplexer_1_out3), .Q(_00011_q), .clk(clock_1_out));  // open: clr
  Register #(.width(32)) _00100 (.D(WD), .en(demultiplexer_1_out4), .Q(_00100_q), .clk(clock_1_out));  // open: clr
  Register #(.width(32)) _00101 (.D(WD), .en(demultiplexer_1_out5), .Q(_00101_q), .clk(clock_1_out));  // open: clr
  Register #(.width(32)) _00110 (.D(WD), .en(demultiplexer_1_out6), .Q(_00110_q), .clk(clock_1_out));  // open: clr
  Register #(.width(32)) _00111 (.D(WD), .en(demultiplexer_1_out7), .Q(_00111_q), .clk(clock_1_out));  // open: clr
  Register #(.width(32)) _01000 (.D(WD), .en(demultiplexer_1_out8), .Q(_01000_q), .clk(clock_1_out));  // open: clr
  Register #(.width(32)) _01001 (.D(WD), .en(demultiplexer_1_out9), .Q(_01001_q), .clk(clock_1_out));  // open: clr
  Register #(.width(32)) _01010 (.D(WD), .en(demultiplexer_1_out10), .Q(_01010_q), .clk(clock_1_out));  // open: clr
  Register #(.width(32)) _01011 (.D(WD), .en(demultiplexer_1_out11), .Q(_01011_q), .clk(clock_1_out));  // open: clr
  Register #(.width(32)) _01100 (.D(WD), .en(demultiplexer_1_out12), .Q(_01100_q), .clk(clock_1_out));  // open: clr
  Register #(.width(32)) _01101 (.D(WD), .en(demultiplexer_1_out13), .Q(_01101_q), .clk(clock_1_out));  // open: clr
  Register #(.width(32)) _01110 (.D(WD), .en(demultiplexer_1_out14), .Q(_01110_q), .clk(clock_1_out));  // open: clr
  Register #(.width(32)) _01111 (.D(WD), .en(demultiplexer_1_out15), .Q(_01111_q), .clk(clock_1_out));  // open: clr
  Register #(.width(32)) _10000 (.D(WD), .en(demultiplexer_1_out16), .Q(_10000_q), .clk(clock_1_out));  // open: clr
  Register #(.width(32)) _10001 (.D(WD), .en(demultiplexer_1_out17), .Q(_10001_q), .clk(clock_1_out));  // open: clr
  Register #(.width(32)) _10010 (.D(WD), .en(demultiplexer_1_out18), .Q(_10010_q), .clk(clock_1_out));  // open: clr
  Register #(.width(32)) _10011 (.D(WD), .en(demultiplexer_1_out19), .Q(_10011_q), .clk(clock_1_out));  // open: clr
  Register #(.width(32)) _10100 (.D(WD), .en(demultiplexer_1_out20), .Q(_10100_q), .clk(clock_1_out));  // open: clr
  Register #(.width(32)) _10101 (.D(WD), .en(demultiplexer_1_out21), .Q(_10101_q), .clk(clock_1_out));  // open: clr
  Register #(.width(32)) _10110 (.D(WD), .en(demultiplexer_1_out22), .Q(_10110_q), .clk(clock_1_out));  // open: clr
  Register #(.width(32)) _10111 (.D(WD), .en(demultiplexer_1_out23), .Q(_10111_q), .clk(clock_1_out));  // open: clr
  Register #(.width(32)) _11000 (.D(WD), .en(demultiplexer_1_out24), .Q(_11000_q), .clk(clock_1_out));  // open: clr
  Register #(.width(32)) _11001 (.D(WD), .en(demultiplexer_1_out25), .Q(_11001_q), .clk(clock_1_out));  // open: clr
  Register #(.width(32)) _11010 (.D(WD), .en(demultiplexer_1_out26), .Q(_11010_q), .clk(clock_1_out));  // open: clr
  Register #(.width(32)) _11011 (.D(WD), .en(demultiplexer_1_out27), .Q(_11011_q), .clk(clock_1_out));  // open: clr
  Register #(.width(32)) _11100 (.D(WD), .en(demultiplexer_1_out28), .Q(_11100_q), .clk(clock_1_out));  // open: clr
  Register #(.width(32)) _11101 (.D(WD), .en(demultiplexer_1_out29), .Q(_11101_q), .clk(clock_1_out));  // open: clr
  Register #(.width(32)) _11110 (.D(WD), .en(demultiplexer_1_out30), .Q(_11110_q), .clk(clock_1_out));  // open: clr
  Register #(.width(32)) _11111 (.D(WD), .en(demultiplexer_1_out31), .clk(clock_1_out));  // open: Q, clr
  Register #(.width(32)) _00000_2 (.D(WD), .en(demultiplexer_2_out0), .Q(_00000_2_q), .clk(clock_1_out));  // open: clr
  Register #(.width(32)) _00001_2 (.D(WD), .en(demultiplexer_2_out1), .Q(_00001_2_q), .clk(clock_1_out));  // open: clr
  Register #(.width(32)) _00010_2 (.D(WD), .en(demultiplexer_2_out2), .Q(_00010_2_q), .clk(clock_1_out));  // open: clr
  Register #(.width(32)) _00011_2 (.D(WD), .en(demultiplexer_2_out3), .Q(_00011_2_q), .clk(clock_1_out));  // open: clr
  Register #(.width(32)) _00100_2 (.D(WD), .en(demultiplexer_2_out4), .Q(_00100_2_q), .clk(clock_1_out));  // open: clr
  Register #(.width(32)) _00101_2 (.D(WD), .en(demultiplexer_2_out5), .Q(_00101_2_q), .clk(clock_1_out));  // open: clr
  Register #(.width(32)) _00110_2 (.D(WD), .en(demultiplexer_2_out6), .Q(_00110_2_q), .clk(clock_1_out));  // open: clr
  Register #(.width(32)) _00111_2 (.D(WD), .en(demultiplexer_2_out7), .Q(_00111_2_q), .clk(clock_1_out));  // open: clr
  Register #(.width(32)) _01000_2 (.D(WD), .en(demultiplexer_2_out8), .Q(_01000_2_q), .clk(clock_1_out));  // open: clr
  Register #(.width(32)) _01001_2 (.D(WD), .en(demultiplexer_2_out9), .Q(_01001_2_q), .clk(clock_1_out));  // open: clr
  Register #(.width(32)) _01010_2 (.D(WD), .en(demultiplexer_2_out10), .Q(_01010_2_q), .clk(clock_1_out));  // open: clr
  Register #(.width(32)) _01011_2 (.D(WD), .en(demultiplexer_2_out11), .Q(_01011_2_q), .clk(clock_1_out));  // open: clr
  Register #(.width(32)) _01100_2 (.D(WD), .en(demultiplexer_2_out12), .Q(_01100_2_q), .clk(clock_1_out));  // open: clr
  Register #(.width(32)) _01101_2 (.D(WD), .en(demultiplexer_2_out13), .Q(_01101_2_q), .clk(clock_1_out));  // open: clr
  Register #(.width(32)) _01110_2 (.D(WD), .en(demultiplexer_2_out14), .Q(_01110_2_q), .clk(clock_1_out));  // open: clr
  Register #(.width(32)) _01111_2 (.D(WD), .en(demultiplexer_2_out15), .Q(_01111_2_q), .clk(clock_1_out));  // open: clr
  Register #(.width(32)) _10000_2 (.D(WD), .en(demultiplexer_2_out16), .Q(_10000_2_q), .clk(clock_1_out));  // open: clr
  Register #(.width(32)) _10001_2 (.D(WD), .en(demultiplexer_2_out17), .Q(_10001_2_q), .clk(clock_1_out));  // open: clr
  Register #(.width(32)) _10010_2 (.D(WD), .en(demultiplexer_2_out18), .Q(_10010_2_q), .clk(clock_1_out));  // open: clr
  Register #(.width(32)) _10011_2 (.D(WD), .en(demultiplexer_2_out19), .Q(_10011_2_q), .clk(clock_1_out));  // open: clr
  Register #(.width(32)) _10100_2 (.D(WD), .en(demultiplexer_2_out20), .Q(_10100_2_q), .clk(clock_1_out));  // open: clr
  Register #(.width(32)) _10101_2 (.D(WD), .en(demultiplexer_2_out21), .Q(_10101_2_q), .clk(clock_1_out));  // open: clr
  Register #(.width(32)) _10110_2 (.D(WD), .en(demultiplexer_2_out22), .Q(_10110_2_q), .clk(clock_1_out));  // open: clr
  Register #(.width(32)) _10111_2 (.D(WD), .en(demultiplexer_2_out23), .Q(_10111_2_q), .clk(clock_1_out));  // open: clr
  Register #(.width(32)) _11000_2 (.D(WD), .en(demultiplexer_2_out24), .Q(_11000_2_q), .clk(clock_1_out));  // open: clr
  Register #(.width(32)) _11001_2 (.D(WD), .en(demultiplexer_2_out25), .Q(_11001_2_q), .clk(clock_1_out));  // open: clr
  Register #(.width(32)) _11010_2 (.D(WD), .en(demultiplexer_2_out26), .Q(_11010_2_q), .clk(clock_1_out));  // open: clr
  Register #(.width(32)) _11011_2 (.D(WD), .en(demultiplexer_2_out27), .Q(_11011_2_q), .clk(clock_1_out));  // open: clr
  Register #(.width(32)) _11100_2 (.D(WD), .en(demultiplexer_2_out28), .Q(_11100_2_q), .clk(clock_1_out));  // open: clr
  Register #(.width(32)) _11101_2 (.D(WD), .en(demultiplexer_2_out29), .Q(_11101_2_q), .clk(clock_1_out));  // open: clr
  Register #(.width(32)) _11110_2 (.D(WD), .en(demultiplexer_2_out30), .Q(_11110_2_q), .clk(clock_1_out));  // open: clr
  Register #(.width(32)) _11111_2 (.D(WD), .en(demultiplexer_2_out31), .clk(clock_1_out));  // open: Q, clr
  assign and_1_out = {32{1'b0}} & _00000_q;  // AND_Gate and_1, 32 bits wide
  assign and_2_out = {32{1'b0}} & _00000_2_q;  // AND_Gate and_2, 32 bits wide
  Multiplexer #(.select(5), .width(32)) multiplexer_1 (
    .in0(and_1_out), .in1(_00001_q), .in2(_00010_q), .in3(_00011_q), .in4(_00100_q), .in5(_00101_q),
    .in6(_00110_q), .in7(_00111_q), .in8(_01000_q), .in9(_01001_q), .in10(_01010_q), .in11(_01011_q),
    .in12(_01100_q), .in13(_01101_q), .in14(_01110_q), .in15(_01111_q), .in16(_10000_q), .in17(_10001_q),
    .in18(_10010_q), .in19(_10011_q), .in20(_10100_q), .in21(_10101_q), .in22(_10110_q), .in23(_10111_q),
    .in24(_11000_q), .in25(_11001_q), .in26(_11010_q), .in27(_11011_q), .in28(_11100_q), .in29(_11101_q),
    .in30(_11110_q), .in31(undriven), .out(LD1), .sel(LR1));  // open: en
  Multiplexer #(.select(5), .width(32)) multiplexer_2 (
    .in0(and_2_out), .in1(_00001_2_q), .in2(_00010_2_q), .in3(_00011_2_q), .in4(_00100_2_q),
    .in5(_00101_2_q), .in6(_00110_2_q), .in7(_00111_2_q), .in8(_01000_2_q), .in9(_01001_2_q),
    .in10(_01010_2_q), .in11(_01011_2_q), .in12(_01100_2_q), .in13(_01101_2_q), .in14(_01110_2_q),
    .in15(_01111_2_q), .in16(_10000_2_q), .in17(_10001_2_q), .in18(_10010_2_q), .in19(_10011_2_q),
    .in20(_10100_2_q), .in21(_10101_2_q), .in22(_10110_2_q), .in23(_10111_2_q), .in24(_11000_2_q),
    .in25(_11001_2_q), .in26(_11010_2_q), .in27(_11011_2_q), .in28(_11100_2_q), .in29(_11101_2_q),
    .in30(_11110_2_q), .in31(undriven_2), .out(LD2), .sel(LR2));  // open: en
  // Probe on LD1
  // Probe on LR1
  // Probe on LD2
  // Probe on LR2
endmodule

module pega_zero (
  input  [31:0] in_1,
  output out_2
);

  nor nor_1 (out_2, in_1[0], in_1[1], in_1[2], in_1[3], in_1[4], in_1[5], in_1[6], in_1[7], in_1[8], in_1[9], in_1[10], in_1[11], in_1[12], in_1[13], in_1[14], in_1[15], in_1[16], in_1[17], in_1[18], in_1[19], in_1[20], in_1[21], in_1[22], in_1[23], in_1[24], in_1[25], in_1[26], in_1[27], in_1[28], in_1[29], in_1[30], in_1[31]);
endmodule

module decodificador (
  input  [31:0] in_1,
  output [5:0] funct,
  output [4:0] shamt,
  output [4:0] rd,
  output [4:0] rt,
  output [15:0] imm,
  output [4:0] rs,
  output [5:0] opcode,
  output [25:0] addr
);


  assign funct = in_1[5:0];
  assign opcode = in_1[31:26];
  assign rd = in_1[15:11];
  assign rs = in_1[25:21];
  assign rt = in_1[20:16];
  assign shamt = in_1[10:6];
endmodule

module extensor (
  input  in_1,
  output [31:0] out_2
);


  assign out_2 = {32{in_1}};
endmodule

module ler_opcode (
  input  [5:0] in_1,
  output RegWrite,
  output RegDst
);

  nand nand_1 (RegDst, in_1[0], in_1[1], in_1[2], in_1[3], in_1[4], in_1[5]);

  assign RegWrite = RegDst;
endmodule

module overflow (
  input  [31:0] a,
  input  [31:0] b,
  input  [31:0] res,
  output overflow
);

  wire and_1_out, and_2_out, not_1_out, not_2_out, not_3_out;

  not not_1 (not_1_out, a[31]);
  not not_2 (not_2_out, b[31]);
  not not_3 (not_3_out, res[31]);
  and and_1 (and_1_out, not_1_out, not_2_out, res[31]);
  and and_2 (and_2_out, a[31], b[31], not_3_out);
  or or_1 (overflow, and_1_out, and_2_out);
endmodule

module overflow_sub (
  input  [31:0] a,
  input  [31:0] b,
  input  [31:0] res,
  output overflow
);

  wire and_1_out, and_2_out, not_1_out, not_2_out, not_3_out;

  not not_1 (not_1_out, a[31]);
  not not_2 (not_2_out, b[31]);
  not not_3 (not_3_out, res[31]);
  and and_1 (and_1_out, not_1_out, b[31], res[31]);
  and and_2 (and_2_out, a[31], not_2_out, not_3_out);
  or or_1 (overflow, and_1_out, and_2_out);
endmodule
